# Fritzing sketch main (saved by Fritzing 0.9.4)
circuit board: 7.87cm x 2.03cm
breadboards: 1

parts:
  TIP120 = npn-Powertransistor [package="TO220 [THT]"]
  78k = Resistor [tolerance=±5% resistance=77.57k package=THT]
  DTH = female pin header, 3 pins [form="♀ (female)"]
  2_2k = Resistor [tolerance=±5% resistance=2.2k package=THT]
  470uF = Capacitor Polarized [package=cpol-radial-100uf-25v]
  Boost = female pin header, 3 pins [form="♀ (female)"]
  Bat = female pin header, 2 pins [form="♀ (female)"]
  Bat_charger = female pin header, 2 pins [form="♀ (female)"]
  SP = female pin header, 2 pins [form="♀ (female)"]
  LED = female pin header, 2 pins [form="♀ (female)"]
  J11 = double row female pin header, 6 pins [form="♀ (female)"]
  B = female pin header, 1 pin [form="♀ (female)"]
  1mF = Capacitor Polarized [package=cpol-radial-100uf-25v]
  2_2k_2 = Resistor [tolerance=±5% resistance=2.2k package=THT]
  Push = female pin header, 2 pins [form="♀ (female)"]
  TPL51010 = Adafruit TPL5110 Power Timer [part_number="Adafruit #3435"]
  SPreg = female pin header, 3 pins [form="♀ (female)"]
  MCU1 = Raspberry Pi Zero

nets:
  N1: TIP120.base, 2_2k.Pin_1
  N2: TIP120.collector, LED.pin2
  N3: TIP120.emitter, 78k.Pin_1, DTH.pin3, 470uF.-, Boost.pin2, Bat.pin2, Bat_charger.pin2, SP.pin1, J11.pin6, 1mF.-, TPL51010.GND, SPreg.pin2, MCU1.pin_6, MCU1.pin_39
  N4: 78k.Pin_0, Push.pin2, TPL51010.DELAY
  N5: DTH.pin1, Boost.pin3, LED.pin1, J11.pin1, 1mF.+, MCU1.pin_2, MCU1.pin_4, MCU1.pin_40
  N6: DTH.pin2, J11.pin2, MCU1.pin_38
  N7: 2_2k.Pin_0, J11.pin4, MCU1.pin_35
  N8: 470uF.+, Bat.pin1, Bat_charger.pin1, TPL51010.VDD, SPreg.pin3
  N9: Boost.pin1, TPL51010.PWROUT
  N10: SP.pin2, SPreg.pin1
  N11: J11.pin3, 2_2k_2.Pin_1, MCU1.pin_36
  N12: J11.pin5, MCU1.pin_37
  N13: B.pin1, Push.pin1
  N14: 2_2k_2.Pin_0, TPL51010.DONE

notes:
  Sticky pi|20200427
  GND
  DAT
  PIEE Lab UBC
  +5V
  Vin
  Bat
  +
  Vo
  G19
  G16
  G20
  G26

custom parts:
  Adafruit TPL5110 Power Timer: With some development boards, low power usage is an afterthought. Especially when price and usability is the main selling point. So what should you do when its time to turn around and make that project of yours run on a battery or solar? Sure you could try to hot-air that regulator off, or you could jerry-rig a relay. Or, use a 555? Ugh, the options aren't that great. The Adafruit TPL5110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
